# Fritzing sketch weather_station_scheme (saved by Fritzing 0.9.5d)
circuit board: 8.46667cm x 5.64444cm
breadboards: 1

parts:
  U1 = NodeMCU V1.0
  AM1 = AM2320 Humidity and Temperature Sensor [part_number="Adafruit #3721"]
  Grove1 = Grove OLED 128x96
  S1 = Pushbutton [package="[SMD]"]
  Part3 = AHT20 BMP280 pressure and humidity breakout
  Part4 = Adafruit TSL2561 [part_number="Adafruit #439"]

nets (from the schematic view):
  N1: U1.D1, AM1.SDA
  N2: U1.D2, S1.Pin_1, S1.Pin_2
  3V3: U1.3V3, AM1.VDD, Part4.VIN
  GND: U1.GND, AM1.GND, S1.Pin_3, S1.Pin_4, Part3.GND, Part4.GND
  N3: U1.D5, Grove1.SCL, Part3.SCL, Part4.SCL
  N4: U1.D6, Part4.SDA

custom parts:
  NodeMCU V1.0: ESP8266 based NodeMCU
  AM2320 Humidity and Temperature Sensor: AM2320 I2C Humidity and Temperature Sensor
  AHT20 BMP280 pressure and humidity breakout: Cheap breakout board for the BMP280, barometric pressure sensor, and AHT20, humidity sensor
  Adafruit TSL2561: The TSL2561 luminosity sensor is an advanced digital light sensor, ideal for use in a wide range of light situations. Compared to low cost CdS cells, this sensor is more precise, allowing for exact lux calculations and can be configured for different gain/timing ranges to detect light ranges from up to 0.1 - 40,000+ Lux on the fly. The best part of this sensor is that it contains both infrared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
